// Digital circuit two_bit_up_down_counter.dig as structural Verilog
module two_bit_up_down_counter (
  input  direction,
  input  clk,
  output Q1,
  output Q0
);

  wire and_1_out, and_2_out, and_3_out, and_4_out, not_1_out, or_1_out, Q0_nq, Q1_nq, xor_1_out;

  not not_1 (not_1_out, direction);
  xor xor_1 (xor_1_out, direction, Q0);
  and and_1 (and_1_out, Q1_nq, Q0_nq, not_1_out);
  and and_2 (and_2_out, Q1_nq, Q0, direction);
  and and_3 (and_3_out, Q1, Q0, not_1_out);
  and and_4 (and_4_out, Q1, Q0_nq, direction);
  or or_1 (or_1_out, and_1_out, and_2_out, and_3_out, and_4_out);
  D_FF u_Q1 (.D(or_1_out), .C(clk), .Q(Q1), .nQ(Q1_nq));
  D_FF u_Q0 (.D(xor_1_out), .C(clk), .Q(Q0), .nQ(Q0_nq));
endmodule
